# Fritzing sketch NosePoke (saved by Fritzing 0.9.3b)
circuit board: 8.46667cm x 5.64444cm
breadboards: 1

parts:
  Part1 = Arduino Uno (Rev3)
  U1 = Optocoupler [package=THT]
  R1 = Resistor [tolerance=±5% resistance=4.7k package=THT]
  R2 = Resistor [tolerance=±5% resistance=6.8k package=THT]
  R3 = Resistor [tolerance=±5% resistance=4.7k package=THT]
  R4 = Resistor [tolerance=±5% resistance=4.7k package=THT]
  R5 = Resistor [tolerance=±5% resistance=6.8k package=THT]
  R6 = Resistor [tolerance=±5% resistance=6.8k package=THT]
  R7 = Resistor [tolerance=±5% resistance=150 power=250mW package=THT]
  R8 = Resistor [tolerance=±5% resistance=150 power=250mW package=THT]
  U2 = Optocoupler [package=THT]
  U5 = GP1A57HR [package=gp1a57hr]
  U6 = GP1A57HR [package=gp1a57hr]
  U7 = GP1A57HR [package=gp1a57hr]
  J1 = Power Jack [package=power_jack_combo]
  L1 = Solenoid
  L2 = Solenoid

nets:
  N1: Part1.D8, R8.Pin_1
  GND: Part1.GND, U1.Pin_2, R1.Pin_0, R3.Pin_0, R4.Pin_0, U2.Pin_2, U5.5, U6.5, U7.5, J1.GND, L1.pin1, L2.pin1
  N2: Part1.D4, R1.Pin_1, R2.Pin_0
  N3: Part1.D5_PWM, R3.Pin_1, R5.Pin_0
  N4: Part1.D6_PWM, R4.Pin_1, R6.Pin_0
  N5: Part1.D7, R7.Pin_1
  N6: U1.Pin_1, R7.Pin_0
  N7: U1.Pin_4, U2.Pin_4, U5.3, U6.3, U7.3, J1.GNDBREAK, J1.PWR
  N8: U1.Pin_6, L2.pin2
  N9: R2.Pin_1, U5.4
  N10: R5.Pin_1, U6.4
  N11: R6.Pin_1, U7.4
  N12: R8.Pin_0, U2.Pin_1
  N13: U2.Pin_6, L1.pin2
