# Fritzing sketch Rotary (saved by Fritzing 0.9.5d)
circuit board: 8.46667cm x 5.64444cm
breadboards: 1

parts:
  Part1 = Arduino Uno (Rev3)
  J1 = Power Jack [package=power_jack_combo]
  CUI-enc1 = AMT103
  U1 = Optocoupler [package=THT]
  R7 = Resistor [tolerance=±5% resistance=150 power=250mW package=THT]
  L1 = Solenoid
  Part2 = Arduino Uno (Rev3) - ICSP
  Pre-Assembled_Female_BNC1 = Pre-Assembled Female BNC
  Pre-Assembled_Female_BNC2 = Pre-Assembled Female BNC
  Pre-Assembled_Female_BNC3 = Pre-Assembled Female BNC
  Pre-Assembled_Female_BNC4 = Pre-Assembled Female BNC

nets:
  N1: Part1.D8, R7.Pin_1
  N2: Part1.D9_PWM, Pre-Assembled_Female_BNC4.PRB
  N3: Part1.D10_PWM/SS, Pre-Assembled_Female_BNC3.PRB
  N4: Part1.D11_PWM/MOSI, Pre-Assembled_Female_BNC2.PRB
  N5: Part1.D12/MISO, Part2.D2
  N6: Part1.D13/SCK, Part2.D4
  GND: Part1.GND, CUI-enc1.GND, U1.Pin_2, Part2.GND, Pre-Assembled_Female_BNC1.GND, Pre-Assembled_Female_BNC2.GND, Pre-Assembled_Female_BNC3.GND, Pre-Assembled_Female_BNC4.GND
  N7: Part1.D2, CUI-enc1.A
  N8: Part1.D3_PWM, CUI-enc1.B
  5V: Part1.5V, CUI-enc1.5V
  N9: J1.GND, L1.pin1
  N10: J1.GNDBREAK, J1.PWR, U1.Pin_4
  N11: U1.Pin_1, R7.Pin_0
  N12: U1.Pin_6, L1.pin2
  N13: Part2.D3_PWM, Pre-Assembled_Female_BNC1.PRB

notes:
  ScanImage Frame Clock (Input)
  ScanImage New File (Output)
  ScanImage Start Acq. (Output)
  ScanImage End Acq. (Output)
